# Fritzing sketch 32u4-programmer (saved by Fritzing 0.9.3b)
breadboards: 1

parts:
  Part1 = Itsy Bitsy 32u4 5V @ 16MHz [part_number="Adafruit #3677"]
  J1 = Piezo Speaker
  U2 = ATTINY13 [package=dip]
  U3 = 74HC595 [package="DIP16 [THT]"]
  U4 = 74HC595 [package="DIP16 [THT]"]
  C1 = Electrolytic Capacitor [capacitance=4.7µF voltage=35V package="100 mil [THT, electrolytic]"]
  C2 = Electrolytic Capacitor [capacitance=4.7µF voltage=35V package="100 mil [THT, electrolytic]"]
  U6 = EEPROM ZIF Socket [package=dil40-6-eeprom_zif_socket]

nets (from the breadboard view):
  GND: Part1.GND, J1.pin1, U2.GND, U3.GND, U3.OE, U4.GND, U4.OE, C2.-, U6.GND
  N1: Part1.D12, U2.PB5(NRES)
  N2: Part1.D11, J1.pin2
  N3: Part1.D10, U6.I/O7
  N4: Part1.D9, U6.I/O6
  N5: Part1.D7, U6.I/O5
  N6: Part1.D5, U6.I/O4
  N7: Part1.SCL, U6.I/O3
  N8: Part1.SDA, U6.I/O2
  N9: Part1.D1, U6.I/O1
  N10: Part1.D0, U6.I/O0
  N11: Part1.MISO, U2.PB1(MISO)
  N12: Part1.MOSI, U2.PB0(MOSI)
  N13: Part1.SCK, U2.PB2(SCK_ADC1)
  N14: Part1.A5, U3.DS
  N15: Part1.A4, U3.ST_CP, U4.ST_CP
  N16: Part1.A3, U3.SH_CP, U4.SH_CP
  N17: Part1.A2, U6.CE
  N18: Part1.A1, U6.OE
  N19: Part1.A0, U6.WE/A11
  VCC: Part1.+5V, U2.VCC, U3.MR, U3.VCC, U4.MR, U4.VCC, C1.+, U6.VCC/A13
  N20: U3.Q1, U6.A7
  N21: U3.Q2, U6.A8
  N22: U3.Q3, U6.A9
  N23: U3.Q4, U6.A10
  N24: U3.Q7', U4.DS
  N25: U4.Q1, U6.A0
  N26: U4.Q2, U6.A1
  N27: U4.Q3, U6.A2
  N28: U4.Q4, U6.A3
  N29: U4.Q5, U6.A4
  N30: U4.Q6, U6.A5
  N31: U4.Q7, U6.A6
  N32: C1.-, C2.+

custom parts:
  Itsy Bitsy 32u4 5V @ 16MHz: What's smaller than a Feather but larger than a Trinket? It's an Itsy Bitsy! Small, powerful, Arduino-compatible - this microcontroller board is perfect when you want something very compact, but still with a bunch of pins. Itsy Bitsy is only 1.4" long by 0.7" wide, but has 6 power pins, 6 analog & digital pins and 17 digital pins. It packs much of the same capability as an Arduino UNO. So it's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
  EEPROM ZIF Socket: Lever-action ZIF socket for 28 to 32-pin EEPROMs. Supports AT28C16, AT28C256, and AT28C040.
